# Fritzing sketch homework (saved by Fritzing 0.9.3b)
breadboards: 1

parts:
  元件1 = Arduino Uno (Rev3)
  S1 = Pushbutton [package="[THT]"]
  J1 = Basic Servo
  J2 = Basic Servo
  LCD1 = LCD screen
  R1 = Rotary Potentiometer (Small) [maximum_resistance=100kΩ package=THT]
  R2 = Photocell (LDR) [package=THT]
  LED1 = LED - 5mm [color="Red (633nm)" package="5 mm [THT]"]
  RE1 = Rotary Encoder [package=THT]

nets:
  N1: 元件1.A0, R2.pin_1
  N2: 元件1.A1, R1.wiper
  N3: 元件1.A3, J1.pulse
  N4: 元件1.D9_PWM, J2.pulse
  N5: 元件1.D11_PWM/MOSI, LCD1.E
  N6: 元件1.D12/MISO, LCD1.RS
  N7: 元件1.D13/SCK, LED1.cathode
  N8: 元件1.D2, LCD1.DB7
  N9: 元件1.D3_PWM, LCD1.DB6
  N10: 元件1.D4, LCD1.DB5
  N11: 元件1.D5_PWM, LCD1.DB4
  N12: 元件1.D6_PWM, S1.Pin_2
  VCC: 元件1.5V, S1.Pin_3, S1.Pin_4, J1.vcc, J2.vcc, LCD1.VDD, LCD1.LED+, R1.leg1, R2.pin_0, LED1.anode
  GND: 元件1.GND, J1.gnd, J2.gnd, LCD1.VSS, LCD1.R/W, LCD1.LED-, R1.leg2, RE1.EncoderPinA
  N13: LCD1.V0, RE1.EncoderPinC
